# Fritzing sketch 3_sensor_humedad_suelo_led_L7Wqv75w5J (saved by Fritzing 0.9.3b)
breadboards: 1

parts:
  Componente5 = Arduino Micro (Rev3)
  Sensor_humedad_suelo = Soil Moisture Sensor
  LED2 = LEDs [package=led10mm]
  R1 = Resistor [tolerance=±5% resistance=220 package=THT]

nets:
  GND: Componente5.GND, Sensor_humedad_suelo.GND, R1.Pin_1
  5V: Componente5.5V, Sensor_humedad_suelo.VCC
  N1: Componente5.A0, Sensor_humedad_suelo.SIG
  N2: Componente5.D13_PWM, LED2.C
